# Fritzing sketch Alpha_Wiring Schematic (saved by Fritzing 0.9.3b)
circuit board: 8.46667cm x 5.64444cm
breadboards: 1

parts:
  SW1 = PowerSwitch Tail II
  UI_LED = RGB LED - (4 legs) [package="5 mm [THT]"]
  R_Red_(TODO_220Ohm) = Resistor [tolerance=±5% resistance=470 package=THT]
  R_Green_(TODO_220Ohm) = Resistor [tolerance=±5% resistance=470 package=THT]
  T-Cobbler_Plus = Adafruit T-Cobbler Plus [part_number="Adafruit #1989 and #2028"]
  R_Blue_(TODO_220Ohm) = Resistor [tolerance=±5% resistance=470 package=THT]
  Matrix_Keypad = Membrane Matrix Keypad

nets:
  N1: SW1.+in, T-Cobbler_Plus.GPIO21
  N2: SW1.-in, T-Cobbler_Plus.GND
  N3: UI_LED.red_cathode, R_Red_(TODO_220Ohm).Pin_0
  N4: UI_LED.common_anode, T-Cobbler_Plus.+5V
  N5: UI_LED.green_cathode, R_Green_(TODO_220Ohm).Pin_0
  N6: UI_LED.blue_cathode, R_Blue_(TODO_220Ohm).Pin_0
  N7: R_Red_(TODO_220Ohm).Pin_1, T-Cobbler_Plus.GPIO26
  N8: R_Green_(TODO_220Ohm).Pin_1, T-Cobbler_Plus.GPIO19
  N9: T-Cobbler_Plus.GPIO13, R_Blue_(TODO_220Ohm).Pin_1
  N10: T-Cobbler_Plus.GPIO18, Matrix_Keypad.1
  N11: T-Cobbler_Plus.GPIO23, Matrix_Keypad.2
  N12: T-Cobbler_Plus.GPIO24, Matrix_Keypad.3
  N13: T-Cobbler_Plus.GPIO25, Matrix_Keypad.4
  N14: T-Cobbler_Plus.GPIO12, Matrix_Keypad.5
  N15: T-Cobbler_Plus.GPIO16, Matrix_Keypad.6
  N16: T-Cobbler_Plus.GPIO20, Matrix_Keypad.7

custom parts:
  Adafruit T-Cobbler Plus: The Raspberry Pi has landed on the Maker World like a 40-GPIO pinned, quad-USB ported, credit card sized bomb of DIY joy. And while you can use most of our great Model B accessories by hooking up our downgrade cable, its probably a good time to upgrade your set up and accessorize using all of the 40 pins. That's why we now carry the Assembled Adafruit Pi T-Cobbler Plus - Breakout + Cable for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
  Membrane Matrix Keypad: Membrane Matrix 3x4 Keypad
